# Fritzing sketch TinyLoadr_Standalone_v4.1.0 (saved by Fritzing 0.8.7b)
circuit board: 5cm x 9cm
breadboards: 1

parts:
  28-Pin_ZIF_Socket = 28-Pin ZIF Socket from SparkFun [part_number=PRT-09175 sticky=false]
  J1 = female pin header, 14 pins [form="♀ (female)"]
  J2 = female pin header, 14 pins [form="♀ (female)"]
  ICSP-10 = double row female pin header, 10 pins [form="♀ (female)"]
  ICSP-6 = double row female pin header, 6 pins [form="♀ (female)"]
  μC_SELECT = double row male pin header, 8 pins [form="♂ (male)"]
  XTAL = Crystal [frequency="16 Mhz" package=SMD]
  IC4 = SO16 [chip_label=IC4 part_number=74FST3257DTR2G package=SO]
  IC3 = SO16 [chip_label=IC3 part_number=74FST3257DTR2G package=SO]
  IC1 = SO16 [chip_label=IC1 part_number=74FST3257DTR2G package=SO]
  IC2 = SO16 [chip_label=IC2 part_number=74FST3257DTR2G package=SO]
  ATtiny24 = ATtiny84/44/24 [chip_label=SOIC-14 package=SOIC-14]
  D1 = Zener Diode [part_number=1N4732A breakdown_voltage=3.6V package="300 mil [THT]"]
  D2 = Zener Diode [part_number=1N4732A breakdown_voltage=3.6V package="300 mil [THT]"]
  C3 = Ceramic Capacitor [capacitance=22pF package="1206 [SMD, multilayer]"]
  C4 = Ceramic Capacitor [capacitance=22pF package="1206 [SMD, multilayer]"]
  R1 = Resistor [tolerance=±5% resistance=1.5k package="1206 [SMD]"]
  C1 = Ceramic Capacitor [capacitance=0.1µF package="1206 [SMD, multilayer]"]
  R2 = Resistor [tolerance=±5% resistance=68 package="1206 [SMD]"]
  R3 = Resistor [tolerance=±5% resistance=68 package="1206 [SMD]"]
  C2 = Ceramic Capacitor [capacitance=0.1µF package="1206 [SMD, multilayer]"]
  BLINK = smd LED [color="Blue (525nm)" package="1206 [SMD]"]
  POWER = smd LED [color="Blue (525nm)" package="1206 [SMD]"]
  R4 = Resistor [tolerance=±5% resistance=680 package="1206 [SMD]"]
  R5 = Resistor [tolerance=±5% resistance=680 package="1206 [SMD]"]
  ATtiny85 = ATTINY13 [package=so]
  R6 = Resistor [tolerance=±5% resistance=10k package="1206 [SMD]"]
  X2 = USB+SHIELD [package=usb-b-pth]
  Part1 = ATtiny84/44/24 [chip_label=SOIC-14 package=SOIC-14]  # not connected
  Part2 = ATtiny2313 / ATtiny4313 [package=SOIC-20]  # not connected

nets:
  ZIF Pin 1: 28-Pin_ZIF_Socket.Pin_1, J1.pin14, IC4.3, IC3.5, IC2.5, IC2.6
  ZIF Pin 2: 28-Pin_ZIF_Socket.Pin_2, J1.pin13, IC3.10, IC3.11
  ZIF Pin 3: 28-Pin_ZIF_Socket.Pin_3, J1.pin12, IC3.13, IC3.14
  ZIF Pin 4: 28-Pin_ZIF_Socket.Pin_4, J1.pin11, IC3.2, IC3.6, IC2.14
  ZIF Pin 5: 28-Pin_ZIF_Socket.Pin_5, J1.pin10, IC2.11
  ZIF Pin 6: 28-Pin_ZIF_Socket.Pin_6, J1.pin9
  ZIF Pin 7: 28-Pin_ZIF_Socket.Pin_7, J1.pin8, IC4.13, IC1.2
  ZIF Pin 8: 28-Pin_ZIF_Socket.Pin_8, J1.pin7, IC1.14
  ZIF Pin 9: 28-Pin_ZIF_Socket.Pin_9, J1.pin6, IC2.10
  ZIF Pin 10: 28-Pin_ZIF_Socket.Pin_10, J1.pin5, IC2.2, IC2.13
  ZIF Pin 11: 28-Pin_ZIF_Socket.Pin_11, J1.pin4
  ZIF Pin 12: 28-Pin_ZIF_Socket.Pin_12, J1.pin3
  ZIF Pin 13: 28-Pin_ZIF_Socket.Pin_13, J1.pin2
  ZIF Pin 14: 28-Pin_ZIF_Socket.Pin_14, J1.pin1
  ZIF Pin 15: 28-Pin_ZIF_Socket.Pin_15, J2.pin1
  ZIF Pin 16: 28-Pin_ZIF_Socket.Pin_16, J2.pin2
  MOSI/ZIF Pin 17: 28-Pin_ZIF_Socket.Pin_17, J2.pin3, ICSP-10.pin1, ICSP-6.pin5, IC4.12, ATtiny85.PB0(MOSI)
  MISO/ZIF Pin 18: 28-Pin_ZIF_Socket.Pin_18, J2.pin4, ICSP-10.pin5, ICSP-6.pin1, IC4.9, ATtiny85.PB1(MISO)
  ZIF Pin 19: 28-Pin_ZIF_Socket.Pin_19, J2.pin5, IC1.11
  ZIF Pin 20: 28-Pin_ZIF_Socket.Pin_20, J2.pin6, IC1.5
  ZIF Pin 21: 28-Pin_ZIF_Socket.Pin_21, J2.pin7
  ZIF Pin 22: 28-Pin_ZIF_Socket.Pin_22, J2.pin8, IC4.10, IC2.3
  ZIF Pin 23: 28-Pin_ZIF_Socket.Pin_23, J2.pin9, IC4.6
  ZIF Pin 24: 28-Pin_ZIF_Socket.Pin_24, J2.pin10
  ZIF Pin 25: 28-Pin_ZIF_Socket.Pin_25, J2.pin11, IC4.14
  ZIF Pin 26: 28-Pin_ZIF_Socket.Pin_26, J2.pin12, IC4.11, R4.Pin_1
  ZIF Pin 27: 28-Pin_ZIF_Socket.Pin_27, J2.pin13, IC4.5
  ZIF Pin 28: 28-Pin_ZIF_Socket.Pin_28, J2.pin14, IC4.2, IC3.3
  RESET: ICSP-10.pin3, ICSP-6.pin3, IC3.7, IC2.7, ATtiny85.PB5(NRES), R6.Pin_0
  SCK: ICSP-10.pin4, ICSP-6.pin2, IC4.7, IC1.9, ATtiny85.PB2(SCK_ADC1)
  GND: ICSP-10.pin6, ICSP-10.pin7, ICSP-10.pin8, ICSP-10.pin9, ICSP-6.pin4, μC_SELECT.pin1, μC_SELECT.pin2, μC_SELECT.pin3, μC_SELECT.pin4, IC4.8, IC3.4, IC3.8, IC1.1, IC1.8, IC1.12, IC2.4, IC2.8, ATtiny24.14, D1.anode, D2.anode, C3.1, C4.1, C1.0, C2.0, BLINK.cathode, POWER.cathode, ATtiny85.GND, X2.GND
  5V: ICSP-10.pin10, ICSP-6.pin6, IC4.4, IC4.16, IC3.16, IC1.4, IC1.7, IC1.16, IC2.16, ATtiny24.1, R1.Pin_0, C1.1, C2.1, R5.Pin_1, ATtiny85.VCC, R6.Pin_1, X2.VBUS
  N1: μC_SELECT.pin5, ATtiny24.7
  N2: μC_SELECT.pin6, ATtiny24.8
  N3: μC_SELECT.pin7, ATtiny24.9
  N4: μC_SELECT.pin8, ATtiny24.12
  XTAL1: XTAL.pin_0, IC3.9, IC2.9, C3.0
  XTAL2: XTAL.pin_1, IC3.12, IC2.12, C4.0
  N5: IC4.1, ATtiny24.3
  N6: IC4.15, ATtiny24.5
  N7: IC3.1, ATtiny24.2
  N8: IC3.15, ATtiny24.6
  N9: IC1.15, ATtiny24.13
  N10: IC2.1, ATtiny24.11
  N11: IC2.15, ATtiny24.10
  N12: D1.cathode, R1.Pin_1, R3.Pin_1, X2.D-
  N13: D2.cathode, R2.Pin_1, X2.D+
  N14: R2.Pin_0, ATtiny85.PB3(ADC3)
  N15: R3.Pin_0, ATtiny85.PB4(ADC2)
  N16: BLINK.anode, R4.Pin_0
  N17: POWER.anode, R5.Pin_0

notes:
  Crystal + Capacitors for ATMega328
  Description: An Arduino shield to be used for programming/bootloading ATtiny
  and ATmega microconrollers.
  Author: Jeff Murchison
  Contact: jeff@jeffmurchison.com
  Date: July 11, 2012
  Version: 1.0
  License:
  This work is licensed under a Creative Commons Attribution-NonCommercial-ShareAlike 3.0 Unported License:
  http://creativecommons.org/licenses/by-nc-sa/3.0/
  You are free to:
  Share — to copy, distribute and transmit the work
  Remix — to adapt the work
  Under the following conditions:
  Attribution — You must attribute the work in the manner specified by the author or licensor (but not in any way that suggests that they endorse you or your use of the work).
  Noncommercial — You may not use this work for commercial purposes.
  Share Alike — If you alter, transform, or build upon this work, you may distribute the resulting work only under the same or similar license to this one.
  ------
  Notes: May require a custom part (ZIF socket).
  If you have any questions, comments, or if you've made some awesome changes to my design, feel free to send me an email!
  You can also BUY one of these shields (provided any are in stock) at:
  https://tindie.com/jeffmurchison/
  .
  Designed By Jeff Murchison
  *4
  *5
  *313
  ATmega
  BLINK LED (*) Pin Map
  *4 - PA1 / D9
  *5 - PB1 / D1
  *313 - PB6 / D15
  ATmega - PC3 / D17
  murchlabs.com
  *
  TinyLoadr AVR
  Programmer v1.0
  ZIF Socket pins - broken out
  28-Pin ZIF Socket
  with Blink LED
  10 and 6-pin ICSP headers
  16MHz Crystal + Caps for programming
  74FST3257DTR2G Quad 2:1 Multiplexers for SPI signal switching.
  ATtiny24/44/84 for controlling multiplexers (selecting which uC to program in the socket)
  ATtiny45/85 to act as USB host and AVR programmer using VUSB and usbtiny firmware.
  Jumper for selecting which uC to program.
  BUILD 4.1.0
  ------------
  -----

custom parts:
  28-Pin ZIF Socket from SparkFun: A 28-pin slim ZIF socket, ordered from Sparkfun.
  ATTINY13: Atmel 8-pin 1kB flash uC
  ATtiny2313 / ATtiny4313: SOIC-20
